# Fritzing sketch Wack-A-Mole (saved by Fritzing 0.9.4)
breadboards: 1

parts:
  Part1 = Arduino Uno (Rev3)
  R1 = Resistor [tolerance=±5% resistance=220 package=THT]
  LED1 = LED - 5mm [color="Red (633nm)" package="5 mm [THT]"]
  S1 = Pushbutton [package="[THT]"]
  LED2 = LED - 5mm [color="Yellow (595nm)" package="5 mm [THT]"]
  LED3 = LED - 5mm [color="Yellow (595nm)" package="5 mm [THT]"]
  S2 = Pushbutton [package="[THT]"]
  S3 = Pushbutton [package="[THT]"]
  LED4 = LED - 5mm [color="Yellow (595nm)" package="5 mm [THT]"]
  S4 = Pushbutton [package="[THT]"]
  LED5 = LED - 5mm [color="Yellow (595nm)" package="5 mm [THT]"]
  S5 = Pushbutton [package="[THT]"]
  R2 = Resistor [tolerance=±5% resistance=1k package=THT]
  R3 = Resistor [tolerance=±5% resistance=1k package=THT]
  R4 = Resistor [tolerance=±5% resistance=1k package=THT]
  R5 = Resistor [tolerance=±5% resistance=1k package=THT]
  R6 = Resistor [tolerance=±5% resistance=1k package=THT]
  R7 = Resistor [tolerance=±5% resistance=220 package=THT]
  R8 = Resistor [tolerance=±5% resistance=220 package=THT]
  R9 = Resistor [tolerance=±5% resistance=220 package=THT]
  R10 = Resistor [tolerance=±5% resistance=220 package=THT]
  LED6 = LED - 5mm [color="Green (570nm)" package="5 mm [THT]"]
  R11 = Resistor [tolerance=±5% resistance=220 package=THT]

nets:
  N1: Part1.D8, LED5.cathode, R10.Pin_0
  N2: Part1.D9_PWM, LED4.anode
  N3: Part1.D10_PWM/SS, LED3.anode
  N4: Part1.D11_PWM/MOSI, LED2.anode
  N5: Part1.D12/MISO, LED1.anode
  N6: Part1.D2, S5.Pin_1, S5.Pin_2, R6.Pin_0
  N7: Part1.D3_PWM, S4.Pin_1, S4.Pin_2, R5.Pin_0
  N8: Part1.D4, S2.Pin_1, S2.Pin_2, R4.Pin_0
  N9: Part1.D5_PWM, S3.Pin_1, S3.Pin_2, R3.Pin_0
  N10: Part1.D6_PWM, S1.Pin_1, S1.Pin_2, R2.Pin_0
  N11: Part1.D7, LED6.anode
  N12: Part1.5V, S1.Pin_3, S1.Pin_4, S2.Pin_3, S2.Pin_4, S3.Pin_3, S3.Pin_4, S4.Pin_3, S4.Pin_4, S5.Pin_3, S5.Pin_4
  N13: Part1.GND, R1.Pin_1, R2.Pin_1, R3.Pin_1, R4.Pin_1, R5.Pin_1, R6.Pin_1, R7.Pin_1, R8.Pin_1, R9.Pin_1, R10.Pin_1, R11.Pin_1
  N14: R1.Pin_0, LED1.cathode
  N15: LED2.cathode, R7.Pin_0
  N16: LED3.cathode, R8.Pin_0
  N17: LED4.cathode, R9.Pin_0
  N18: LED6.cathode, R11.Pin_0
